# Fritzing sketch Transistor_Led (saved by Fritzing 0.9.4)
breadboards: 1

parts:
  Componente1 = Arduino Uno (Rev3)
  LED1 = LED - 5mm [color="Red (633nm)" package="5 mm [THT]"]
  R2 = Rotary Potentiometer (Small) [maximum_resistance=100kΩ package=THT]
  R1 = Resistor [tolerance=±5% resistance=220 package=THT]
  Q1 = NPN-Transistor [package="TO92 [THT]"]
  R3 = Resistor [tolerance=±5% resistance=220 package=THT]

nets:
  N1: Componente1.A0, R2.wiper
  N2: Componente1.D9_PWM, R3.Pin_1
  N3: Componente1.GND, R2.leg1, R1.Pin_1
  N4: Componente1.5V, R2.leg2, Q1.E
  N5: LED1.cathode, R1.Pin_0
  N6: LED1.anode, Q1.C
  N7: Q1.B, R3.Pin_0
