# Fritzing sketch 3bits (saved by Fritzing 0.9.4)
breadboards: 1

parts:
  R1 = Rotary Potentiometer (Small) [maximum_resistance=100kΩ package=THT]
  R2 = Resistor [tolerance=±5% resistance=220 package=THT]
  R3 = Resistor [tolerance=±5% resistance=220 package=THT]
  R4 = Resistor [tolerance=±5% resistance=220 package=THT]
  LED1 = LED - 5mm [color="Red (633nm)" package="5 mm [THT]"]
  LED2 = LED - 5mm [color="Red (633nm)" package="5 mm [THT]"]
  LED3 = LED - 5mm [color="Red (633nm)" package="5 mm [THT]"]
  Componente1 = Arduino Uno (Rev3)

nets:
  N1: R1.leg1, R2.Pin_0, R3.Pin_0, R4.Pin_0, Componente1.GND
  N2: R1.wiper, Componente1.A0
  N3: R1.leg2, Componente1.5V
  N4: R2.Pin_1, LED3.cathode
  N5: R3.Pin_1, LED1.cathode
  N6: R4.Pin_1, LED2.cathode
  N7: LED1.anode, Componente1.D3_PWM
  N8: LED2.anode, Componente1.D5_PWM
  N9: LED3.anode, Componente1.D8
