# Fritzing sketch 5Leds (saved by Fritzing 0.9.4)
breadboards: 1

parts:
  Componente1 = Arduino Uno (Rev3)
  R1 = Resistor [tolerance=±5% resistance=220 package=THT]
  R2 = Resistor [tolerance=±5% resistance=220 package=THT]
  R3 = Resistor [tolerance=±5% resistance=220 package=THT]
  R4 = Resistor [tolerance=±5% resistance=220 package=THT]
  R5 = Resistor [tolerance=±5% resistance=220 package=THT]
  LED1 = LED - 5mm [color="Red (633nm)" package="5 mm [THT]"]
  LED2 = LED - 5mm [color="Red (633nm)" package="5 mm [THT]"]
  LED3 = LED - 5mm [color="Red (633nm)" package="5 mm [THT]"]
  LED4 = LED - 5mm [color="Red (633nm)" package="5 mm [THT]"]
  LED5 = LED - 5mm [color="Red (633nm)" package="5 mm [THT]"]

nets:
  N1: Componente1.GND, R1.Pin_1, R2.Pin_1, R3.Pin_1, R4.Pin_1, R5.Pin_1
  N2: Componente1.D0/RX, LED1.anode
  N3: Componente1.D1/TX, LED2.anode
  N4: Componente1.D2, LED3.anode
  N5: Componente1.D3_PWM, LED4.anode
  N6: Componente1.D4, LED5.anode
  N7: R1.Pin_0, LED3.cathode
  N8: R2.Pin_0, LED2.cathode
  N9: R3.Pin_0, LED4.cathode
  N10: R4.Pin_0, LED1.cathode
  N11: R5.Pin_0, LED5.cathode
