# Fritzing sketch BarraGrafica (saved by Fritzing 0.9.4)
breadboards: 1

parts:
  Componente1 = Arduino Uno (Rev3)
  R1 = Resistor [tolerance=±5% resistance=220 package=THT]
  R2 = Resistor [tolerance=±5% resistance=220 package=THT]
  R3 = Resistor [tolerance=±5% resistance=220 package=THT]
  R4 = Resistor [tolerance=±5% resistance=220 package=THT]
  R5 = Resistor [tolerance=±5% resistance=220 package=THT]
  LED1 = LED - 5mm [color="Red (633nm)" package="5 mm [THT]"]
  LED2 = LED - 5mm [color="Red (633nm)" package="5 mm [THT]"]
  LED3 = LED - 5mm [color="Red (633nm)" package="5 mm [THT]"]
  LED4 = LED - 5mm [color="Red (633nm)" package="5 mm [THT]"]
  LED5 = LED - 5mm [color="Red (633nm)" package="5 mm [THT]"]
  LED6 = LED - 5mm [color="Red (633nm)" package="5 mm [THT]"]
  LED7 = LED - 5mm [color="Red (633nm)" package="5 mm [THT]"]
  LED8 = LED - 5mm [color="Red (633nm)" package="5 mm [THT]"]
  R6 = Resistor [tolerance=±5% resistance=220 package=THT]
  R7 = Resistor [tolerance=±5% resistance=220 package=THT]
  R8 = Resistor [tolerance=±5% resistance=220 package=THT]
  R9 = Rotary Potentiometer (Small) [maximum_resistance=100kΩ package=THT]

nets:
  N1: Componente1.A0, R9.wiper
  N2: Componente1.D0/RX, LED1.anode
  N3: Componente1.D1/TX, LED2.anode
  N4: Componente1.D2, LED3.anode
  N5: Componente1.D3_PWM, LED4.anode
  N6: Componente1.D4, LED5.anode
  N7: Componente1.D5_PWM, LED6.anode
  N8: Componente1.D6_PWM, LED7.anode
  N9: Componente1.D7, LED8.anode
  N10: Componente1.5V, R9.leg2
  N11: Componente1.GND, R1.Pin_1, R2.Pin_1, R3.Pin_1, R4.Pin_1, R5.Pin_1, R6.Pin_0, R7.Pin_1, R8.Pin_1, R9.leg1
  N12: R1.Pin_0, LED3.cathode
  N13: R2.Pin_0, LED2.cathode
  N14: R3.Pin_0, LED4.cathode
  N15: R4.Pin_0, LED1.cathode
  N16: R5.Pin_0, LED5.cathode
  N17: LED6.cathode, R7.Pin_0
  N18: LED7.cathode, R8.Pin_0
  N19: LED8.cathode, R6.Pin_1
