# Fritzing sketch PushBoton (saved by Fritzing 0.9.4)
breadboards: 1

parts:
  S1 = Pushbutton [package="[THT]"]
  Componente1 = Arduino Uno (Rev3)

nets:
  N1: S1.Pin_1, S1.Pin_2, Componente1.D4
  N2: S1.Pin_3, S1.Pin_4, Componente1.GND
