# Fritzing sketch XOR (saved by Fritzing 0.9.4)
breadboards: 1

parts:
  Componente1 = Arduino Uno (Rev3)
  S1 = Pushbutton [package="[THT]"]
  S2 = Pushbutton [package="[THT]"]
  LED1 = LED - 5mm [color="Red (633nm)" package="5 mm [THT]"]
  R1 = Resistor [tolerance=±5% resistance=220 package=THT]

nets:
  N1: Componente1.D2, S1.Pin_3, S1.Pin_4
  N2: Componente1.D4, S2.Pin_3, S2.Pin_4
  N3: Componente1.D7, LED1.anode
  N4: Componente1.GND, S1.Pin_1, S1.Pin_2, S2.Pin_1, S2.Pin_2, R1.Pin_1
  N5: LED1.cathode, R1.Pin_0
