# Fritzing sketch Motor_DC (saved by Fritzing 0.9.4)
breadboards: 1

parts:
  Componente1 = Arduino Uno (Rev3)
  IC1 = L293D [package=THT]
  BAT1 = BC9VPC [package=bc9vpc]
  M1 = DC Motor

nets:
  N1: Componente1.GND, IC1.0V, BAT1.V+
  N2: Componente1.D2, IC1.In_2
  N3: Componente1.D3_PWM, IC1.In_1
  N4: Componente1.D6_PWM, IC1.Enable_1
  N5: Componente1.5V, IC1.+V
  N6: IC1.Out_1_(_Controlled_by_Enable_1_), M1.pin_2
  N7: IC1.Out_2_(_Controlled_by_Enable_1_), M1.pin_1
  N8: IC1.+Vmotor, BAT1.V-
