# Fritzing sketch Servo (saved by Fritzing 0.9.4)
circuit board: 6.88566cm x 5.36311cm
breadboards: 1

parts:
  J1 = Basic Servo
  R1 = Rotary Potentiometer (Small) [maximum_resistance=100kΩ package=THT]
  Arduino2 = Arduino Uno (Rev3)

nets:
  GND: J1.gnd, R1.leg2, Arduino2.GND
  VCC: J1.vcc, R1.leg1, Arduino2.5V
  N1: J1.pulse, Arduino2.D9_PWM
  N2: R1.wiper, Arduino2.A2
