# Fritzing sketch StepMotor (saved by Fritzing 0.9.4)
breadboards: 1

parts:
  LED1 = LED - 5mm [color="Yellow (585nm)" package="5 mm [THT]"]
  LED2 = LED - 5mm [color="Yellow (585nm)" package="5 mm [THT]"]
  LED3 = LED - 5mm [color="Green (555nm)" package="5 mm [THT]"]
  LED4 = LED - 5mm [color="Green (555nm)" package="5 mm [THT]"]
  R1 = Resistor [tolerance=±5% resistance=220 package=THT]
  R2 = Resistor [tolerance=±5% resistance=220 package=THT]
  R3 = Resistor [tolerance=±5% resistance=220 package=THT]
  R4 = Resistor [tolerance=±5% resistance=220 package=THT]
  IC1 = L293D [package=THT]
  Componente1 = Arduino Uno (Rev3)
  S1 = Pushbutton [package="[THT]"]
  S2 = Pushbutton [package="[THT]"]

nets:
  N1: LED1.cathode, R1.Pin_1
  N2: LED1.anode, IC1.Out_4_(_Controlled_by_Enable_2_)
  N3: LED2.cathode, R3.Pin_1
  N4: LED2.anode, IC1.Out_1_(_Controlled_by_Enable_1_)
  N5: LED3.cathode, R2.Pin_1
  N6: LED3.anode, IC1.Out_3_(_Controlled_by_Enable_2_)
  N7: LED4.cathode, R4.Pin_1
  N8: LED4.anode, IC1.Out_2_(_Controlled_by_Enable_1_)
  N9: R1.Pin_0, R2.Pin_0, R3.Pin_0, R4.Pin_0, IC1.0V, Componente1.GND, S1.Pin_3, S1.Pin_4, S2.Pin_3, S2.Pin_4
  N10: IC1.Enable_1, IC1.+Vmotor, IC1.Enable_2, IC1.+V, Componente1.5V
  N11: IC1.In_1, Componente1.D1/TX
  N12: IC1.In_2, Componente1.D0/RX
  N13: IC1.In_3, Componente1.D2
  N14: IC1.In_4, Componente1.D3_PWM
  N15: Componente1.D4, S1.Pin_1, S1.Pin_2
  N16: Componente1.D5_PWM, S2.Pin_1, S2.Pin_2
