# Fritzing sketch ContadorPushBotton (saved by Fritzing 0.9.4)
circuit board: 8.46667cm x 5.64444cm
breadboards: 1

parts:
  Componente1 = Arduino Uno (Rev3)
  R5 = Resistor [tolerance=±5% resistance=220 package=THT]
  R6 = Resistor [tolerance=±5% resistance=220 package=THT]
  R7 = Resistor [tolerance=±5% resistance=220 package=THT]
  R8 = Resistor [tolerance=±5% resistance=220 package=THT]
  R9 = Resistor [tolerance=±5% resistance=220 package=THT]
  LED1 = LED - 5mm [color="Red (633nm)" package="5 mm [THT]"]
  LED2 = LED - 5mm [color="Red (633nm)" package="5 mm [THT]"]
  LED3 = LED - 5mm [color="Red (633nm)" package="5 mm [THT]"]
  LED4 = LED - 5mm [color="Red (633nm)" package="5 mm [THT]"]
  LED5 = LED - 5mm [color="Red (633nm)" package="5 mm [THT]"]
  LED6 = LED - 5mm [color="Red (633nm)" package="5 mm [THT]"]
  LED7 = LED - 5mm [color="Red (633nm)" package="5 mm [THT]"]
  LED8 = LED - 5mm [color="Red (633nm)" package="5 mm [THT]"]
  R10 = Resistor [tolerance=±5% resistance=220 package=THT]
  R11 = Resistor [tolerance=±5% resistance=220 package=THT]
  R12 = Resistor [tolerance=±5% resistance=220 package=THT]
  S1 = Pushbutton [package="[THT]"]
  S2 = Pushbutton [package="[THT]"]
  S3 = Pushbutton [package="[THT]"]

nets:
  N1: Componente1.D8, S1.Pin_1, S1.Pin_2
  N2: Componente1.D9_PWM, S2.Pin_1, S2.Pin_2
  N3: Componente1.D10_PWM/SS, S3.Pin_1, S3.Pin_2
  N4: Componente1.GND, R5.Pin_1, R6.Pin_1, R7.Pin_1, R8.Pin_1, R9.Pin_1, R10.Pin_1, R11.Pin_1, R12.Pin_1, S1.Pin_3, S1.Pin_4, S2.Pin_3, S2.Pin_4, S3.Pin_3, S3.Pin_4
  N5: Componente1.D0/RX, LED1.anode
  N6: Componente1.D1/TX, LED5.anode
  N7: Componente1.D2, LED4.anode
  N8: Componente1.D3_PWM, LED3.anode
  N9: Componente1.D4, LED2.anode
  N10: Componente1.D5_PWM, LED8.anode
  N11: Componente1.D6_PWM, LED7.anode
  N12: Componente1.D7, LED6.anode
  N13: R5.Pin_0, LED2.cathode
  N14: R6.Pin_0, LED3.cathode
  N15: R7.Pin_0, LED4.cathode
  N16: R8.Pin_0, LED5.cathode
  N17: R9.Pin_0, LED1.cathode
  N18: LED6.cathode, R10.Pin_0
  N19: LED7.cathode, R11.Pin_0
  N20: LED8.cathode, R12.Pin_0
