# Fritzing sketch ContadorExa (saved by Fritzing 0.9.4)
circuit board: 8.46667cm x 5.64444cm
breadboards: 1

parts:
  S1 = Pushbutton [package="[THT]"]
  S2 = Pushbutton [package="[THT]"]
  S3 = Pushbutton [package="[THT]"]
  S4 = Pushbutton [package="[THT]"]
  Componente1 = Arduino Uno (Rev3)
  DI1 = 7-Segment LED Display [package=THT]
  R1 = Resistor [tolerance=±5% resistance=220 package=THT]
  R2 = Resistor [tolerance=±5% resistance=220 package=THT]

nets:
  N1: S1.Pin_1, S1.Pin_2, Componente1.D11_PWM/MOSI
  N2: S1.Pin_3, S1.Pin_4, S2.Pin_3, S2.Pin_4, S3.Pin_3, S3.Pin_4, S4.Pin_3, S4.Pin_4, Componente1.GND, R1.Pin_1, R2.Pin_0
  N3: S2.Pin_1, S2.Pin_2, Componente1.D10_PWM/SS
  N4: S3.Pin_1, S3.Pin_2, Componente1.D9_PWM
  N5: S4.Pin_1, S4.Pin_2, Componente1.D8
  N6: Componente1.D0/RX, DI1.cathodeA
  N7: Componente1.D1/TX, DI1.cathodeB
  N8: Componente1.D2, DI1.cathodeC
  N9: Componente1.D3_PWM, DI1.cathodeD
  N10: Componente1.D4, DI1.cathodeE
  N11: Componente1.D5_PWM, DI1.cathodeG
  N12: Componente1.D6_PWM, DI1.cathodeF
  N13: Componente1.D7, DI1.cathodeDP
  N14: DI1.commAnode#2, R1.Pin_0
  N15: DI1.commAnode#7, R2.Pin_1
