# Fritzing sketch SensorLDR (saved by Fritzing 0.9.4)
circuit board: 6.88566cm x 5.36311cm
breadboards: 1

parts:
  R5 = Photocell (LDR) [package=THT]
  R6 = Resistor [tolerance=±5% resistance=10k package=THT]
  Arduino1 = Arduino Uno (Rev3)
  LED1 = LED - 5mm [color="Red (633nm)" package="5 mm [THT]"]
  R7 = Resistor [tolerance=±5% resistance=220 package=THT]

nets:
  N1: R5.pin_0, Arduino1.5V
  N2: R5.pin_1, R6.Pin_0, Arduino1.A2
  N3: R6.Pin_1, Arduino1.GND, R7.Pin_1
  N4: Arduino1.D11_PWM/MOSI, LED1.anode
  N5: LED1.cathode, R7.Pin_0
