# Fritzing sketch Temperatura_LCD (saved by Fritzing 0.9.4)
breadboards: 1

parts:
  Componente1 = Arduino Uno (Rev3)
  LCD1 = LCD screen
  U2 = POT [package=pot_mammoth]
  T2 = LM35 Temperature Sensor [package="TO92 [THT]"]
  R1 = Resistor [tolerance=±5% resistance=220 package=THT]

nets:
  N1: Componente1.A0, T2.Vout
  N2: Componente1.D11_PWM/MOSI, LCD1.E
  N3: Componente1.D12/MISO, LCD1.RS
  N4: Componente1.D2, LCD1.DB7
  N5: Componente1.D3_PWM, LCD1.DB6
  N6: Componente1.D4, LCD1.DB5
  N7: Componente1.D5_PWM, LCD1.DB4
  5V: Componente1.5V, LCD1.VDD, LCD1.LED+, U2.S, T2.+Vs
  GND: Componente1.GND, LCD1.VSS, LCD1.R/W, U2.E, T2.GND, R1.Pin_0
  N8: LCD1.V0, U2.A
  N9: LCD1.LED-, R1.Pin_1
