# Fritzing sketch Ultrasonico (saved by Fritzing 0.9.4)
breadboards: 1

parts:
  Componente1 = Arduino Uno (Rev3)
  hc-sr1 = hc-sr04
  R1 = Resistor [tolerance=±5% resistance=220 package=THT]
  LED1 = LED - 5mm [color="Red (633nm)" package="5 mm [THT]"]

nets:
  N1: Componente1.D8, hc-sr1.Trig
  N2: Componente1.D13/SCK, LED1.anode
  GND: Componente1.GND, hc-sr1.GND, R1.Pin_1
  N3: Componente1.D7, hc-sr1.Echo
  5V: Componente1.5V, hc-sr1.VCC
  N4: R1.Pin_0, LED1.cathode
